# Fritzing sketch Shield+lcdI2C (saved by Fritzing 0.9.3b)

parts:
  Composant1 = LCD1602-I2C
  Componente4 = Base Shield V2

nets:
  N1: Composant1.GND, Componente4.pin_124
  N2: Composant1.VCC, Componente4.pin_125
  N3: Composant1.SDA, Componente4.pin_126
  N4: Composant1.SCL, Componente4.pin_127

custom parts:
  LCD1602-I2C: A standard character display, usually with 2x16 characters. Comes in many colors with LCM1602 IIC attached.
